# Fritzing sketch KY-015 (saved by Fritzing 0.9.3b)
breadboards: 1

parts:
  Componente2 = Humidity Sensor - HIH-4030 Breakout
  Componente3 = Arduino Nano (Rev3.0)

nets:
  GND: Componente2.GND, Componente3.GND
  N1: Componente2.OUT, Componente3.D8
  VCC: Componente2.VCC, Componente3.5V
